// Logisim project novo_neander.circ as structural Verilog: 1 circuit, main circuit main
module main (
  input  reset,
  input  count_load,
  input  en_ULA,
  output out_4,
  output load,
  output soma,
  output sub,
  output mult,
  output jump,
  output jumpN,
  output jumpZ,
  output out_12
);

  wire clock_out, comparator_1_eq, not_1_out, not_2_out;
  wire [1:0] register_1_q;
  wire [3:0] ACC_q, adder_1_out, dummy_q, multiplexer_1_out, multiplier_1_out, PC_q, subtractor_1_out;
  wire [7:0] ram_1_data, RDM_q;

  not not_1 (not_1_out, reset);
  Clock clock (.out(clock_out));
  Counter #(.width(4), .max('hf)) PC (
    .load(not_2_out), .D(dummy_q), .count(count_load), .Q(PC_q), .clk(clock_out), .clr(not_1_out));  // open: carry
  not not_2 (not_2_out, count_load);
  Adder #(.width(4)) adder_1 (.a(ACC_q), .b(dummy_q), .out(adder_1_out));  // open: cin, cout
  Subtractor #(.width(4)) subtractor_1 (.a(ACC_q), .b(dummy_q), .out(subtractor_1_out));  // open: bin, bout
  Multiplier #(.width(4)) multiplier_1 (.a(ACC_q), .b(dummy_q), .out(multiplier_1_out));  // open: cin, cout
  Multiplexer #(.select(2), .width(4), .enable("false")) multiplexer_1 (
    .in0(dummy_q), .in1(adder_1_out), .in2(subtractor_1_out), .in3(multiplier_1_out),
    .out(multiplexer_1_out), .sel(register_1_q));
  RAM #(.addrWidth(4)) ram_1 (.addr(PC_q), .data(ram_1_data));  // open: sel, clk, ld, clr
  Comparator #(.width(4)) comparator_1 (.a(multiplexer_1_out), .b(4'b0000), .eq(comparator_1_eq));  // open: gt, lt
  Register RDM (.D(ram_1_data), .Q(RDM_q), .clk(clock_out), .clr(not_1_out));  // open: en
  Register #(.width(1)) Z (.D(comparator_1_eq), .en(en_ULA), .Q(out_4), .clk(clock_out), .clr(not_1_out));
  Register #(.width(4)) ACC (.D(multiplexer_1_out), .en(en_ULA), .Q(ACC_q), .clk(clock_out), .clr(not_1_out));
  Register #(.width(1)) N (.D(multiplexer_1_out[3]), .en(en_ULA), .Q(out_12), .clk(clock_out), .clr(not_1_out));
  Decoder #(.select(4), .enable("false")) decoder_1 (
    .out0(load), .out1(soma), .out2(sub), .out3(mult), .out4(jump), .out5(jumpN), .out6(jumpZ),
    .sel(RDM_q[7:4]));  // open: out7, out8, out9, out10, out11, out12, out13, out14, out15
  Register #(.width(4)) dummy (.D(RDM_q[3:0]), .Q(dummy_q), .clk(clock_out));  // open: en, clr
  Register #(.width(2)) register_1 (.D(RDM_q[5:4]), .Q(register_1_q), .clk(clock_out));  // open: en, clr

  // Notes on the sheet:
  //   0000
  //   0001
  //   0010
  //   0011
  //   0100
  //   0101
  //   0110
endmodule
